// Logisim project Assign_1.circ as structural Verilog: 1 circuit, main circuit main
module main (
  input  in_1
);

  wire and_1_out, and_2_out, and_3_out, and_4_out, and_5_out, and_6_out, and_7_out, and_8_out, and_9_out,
       and_10_out, and_11_out, and_12_out, and_13_out, and_14_out, and_15_out, and_16_out, and_17_out,
       and_18_out, and_19_out, and_20_out, and_21_out, and_22_out, and_23_out, and_24_out, and_25_out,
       and_26_out, and_29_out, and_30_out, and_31_out, and_32_out, and_33_out, and_34_out, and_35_out,
       and_36_out, and_37_out, and_38_out, and_39_out, and_40_out, and_41_out, and_42_out, and_43_out,
       and_44_out, and_45_out, and_46_out, and_47_out, and_48_out, and_49_out, and_50_out, and_51_out,
       and_52_out, and_53_out, and_54_out, and_55_out, and_56_out, and_57_out, and_58_out, and_59_out,
       and_60_out, buffer_1_out, buffer_2_out, buffer_3_out, buffer_4_out, buffer_5_out, buffer_6_out,
       buffer_7_out, buffer_8_out, buffer_9_out, buffer_10_out, buffer_11_out, buffer_12_out, buffer_13_out,
       buffer_14_out, buffer_15_out, buffer_16_out, buffer_17_out, buffer_18_out, buffer_19_out,
       buffer_20_out, d_ff_2_q, d_ff_2_qn, d_ff_3_q, d_ff_4_q, d_ff_5_q, d_ff_6_q, d_ff_7_q, d_ff_8_q,
       d_ff_9_q, d_ff_10_q, d_ff_11_q, d_ff_12_q, j_k_ff_1_q, j_k_ff_2_qn, j_k_ff_3_qn, j_k_ff_4_qn,
       j_k_ff_6_qn, j_k_ff_7_qn, j_k_ff_8_qn, nor_1_out, nor_2_out, not_1_out, not_2_out, not_3_out,
       not_4_out, not_5_out, not_6_out, not_7_out, not_8_out, not_9_out, not_10_out, not_11_out, not_12_out,
       not_13_out, not_14_out, not_15_out, not_16_out, not_17_out, not_18_out, not_19_out, not_20_out,
       not_21_out, not_22_out, not_23_out, not_24_out, not_25_out, not_26_out, Off_Button_out, On_Button_out,
       or_1_out, or_2_out, or_3_out, or_4_out, or_5_out, or_6_out, or_7_out, or_8_out, or_9_out, or_10_out,
       or_11_out, or_12_out, or_13_out, or_14_out, or_15_out, or_16_out, or_17_out, or_18_out, or_19_out,
       or_20_out, or_21_out, or_22_out, Pause_Play_out, Previous_Track_out, reset_volume_out, Skip_Track_out,
       Volume_Down_out, Volume_Up_out, xor_1_out;
  wire [3:0] and_27_out, and_28_out, j_k_ff_2_q, j_k_ff_6_q;
  wire [3:3] d_ff_1_q;

  LED Play_Light (.in(and_10_out));
  LED Pause_Light (.in(and_6_out));
  LED On_Light (.in(d_ff_1_q[3]));
  Button On_Button (.out(On_Button_out));
  Button Off_Button (.out(Off_Button_out));
  Button Pause_Play (.out(Pause_Play_out));
  Button Volume_Up (.out(Volume_Up_out));
  Button Volume_Down (.out(Volume_Down_out));
  Button reset_volume (.out(reset_volume_out));
  Button Skip_Track (.out(Skip_Track_out));
  Button Previous_Track (.out(Previous_Track_out));
  and and_1 (and_1_out, d_ff_1_q[3], or_4_out);
  D_Flip_Flop d_ff_1 (.Q(d_ff_1_q[3]), .preset(On_Button_out), .reset(Off_Button_out));  // open: D, clk, Qn
  and and_2 (and_2_out, d_ff_1_q[3], Pause_Play_out);
  not not_1 (not_1_out, Pause_Play_out);
  buf buffer_1 (buffer_1_out, and_1_out);
  buf buffer_2 (buffer_2_out, buffer_1_out);
  and and_3 (and_3_out, d_ff_1_q[3], Volume_Up_out);
  and and_4 (and_4_out, d_ff_1_q[3], Volume_Down_out);
  nor nor_1 (nor_1_out, nor_2_out, Skip_Track_out);
  buf buffer_3 (buffer_3_out, buffer_6_out);
  buf buffer_4 (buffer_4_out, buffer_3_out);
  buf buffer_5 (buffer_5_out, buffer_2_out);
  buf buffer_6 (buffer_6_out, buffer_5_out);
  D_Flip_Flop d_ff_2 (.D(and_2_out), .clk(and_2_out), .Q(d_ff_2_q), .Qn(d_ff_2_qn), .reset(or_1_out));  // open: preset
  or or_1 (or_1_out, Off_Button_out, and_5_out);
  and and_5 (and_5_out, Pause_Play_out, and_8_out);
  J_K_Flip_Flop j_k_ff_1 (.Q(j_k_ff_1_q), .preset(and_3_out), .reset(and_4_out));  // open: J, K, clk, Qn
  nor nor_2 (nor_2_out, Previous_Track_out, nor_1_out);
  and and_6 (and_6_out, d_ff_1_q[3], d_ff_2_qn);
  D_Flip_Flop d_ff_3 (.D(d_ff_2_q), .clk(not_1_out), .Q(d_ff_3_q), .reset(Off_Button_out));  // open: Qn, preset
  and and_7 (and_7_out, j_k_ff_1_q, j_k_ff_1_q);
  or or_2 (or_2_out, and_7_out, and_9_out);
  or or_3 (or_3_out, and_3_out, and_4_out);
  not not_2 (not_2_out, or_3_out);
  buf buffer_7 (buffer_7_out, buffer_4_out);
  buf buffer_8 (buffer_8_out, buffer_7_out);
  buf buffer_9 (buffer_9_out, buffer_8_out);
  not not_3 (not_3_out, and_6_out);
  and and_8 (and_8_out, d_ff_1_q[3], d_ff_3_q);
  not not_4 (not_4_out, j_k_ff_1_q);
  and and_9 (and_9_out, not_4_out, d_ff_5_q);
  D_Flip_Flop d_ff_4 (.D(or_2_out), .clk(not_2_out), .Q(d_ff_4_q), .reset(reset_volume_out));  // open: Qn, preset
  buf buffer_10 (buffer_10_out, buffer_9_out);
  buf buffer_11 (buffer_11_out, buffer_10_out);
  buf buffer_12 (buffer_12_out, buffer_11_out);
  xor xor_1 (xor_1_out, Skip_Track_out, Previous_Track_out);
  and and_10 (and_10_out, not_3_out, and_8_out);
  or or_4 (or_4_out, xor_1_out, d_ff_9_q);
  Hex_Digit_Display hex_digit_display_1 (.value(and_28_out));  // open: dp
  LED led_1 (.in(and_23_out));
  LED led_2 (.in(and_22_out));
  LED led_3 (.in(and_21_out));
  LED led_4 (.in(and_19_out));
  LED led_5 (.in(and_18_out));
  LED led_6 (.in(and_15_out));
  LED led_7 (.in(and_14_out));
  LED led_8 (.in(and_12_out));
  Hex_Digit_Display hex_digit_display_2 (.value(and_27_out));  // open: dp
  LedBar Volume (
    .led0(and_12_out), .led1(and_14_out), .led2(and_15_out), .led3(and_18_out), .led4(and_19_out),
    .led5(and_21_out), .led6(and_22_out), .led7(and_23_out));
  and and_11 (and_11_out, j_k_ff_1_q, d_ff_4_q);
  J_K_Flip_Flop j_k_ff_2 (
    .J(d_ff_1_q[3]), .K(d_ff_1_q[3]), .clk(buffer_12_out), .Q(j_k_ff_2_q[0]), .Qn(j_k_ff_2_qn),
    .preset(and_37_out), .reset(and_36_out));
  and and_12 (and_12_out, d_ff_1_q[3], d_ff_4_q);
  and and_13 (and_13_out, not_4_out, d_ff_6_q);
  or or_5 (or_5_out, and_11_out, and_13_out);
  D_Flip_Flop d_ff_5 (.D(or_5_out), .clk(not_2_out), .Q(d_ff_5_q), .reset(reset_volume_out));  // open: Qn, preset
  not not_5 (not_5_out, nor_2_out);
  and and_14 (and_14_out, d_ff_1_q[3], d_ff_5_q);
  and and_15 (and_15_out, d_ff_1_q[3], d_ff_6_q);
  and and_16 (and_16_out, nor_2_out, j_k_ff_2_q[0]);
  and and_17 (and_17_out, j_k_ff_2_qn, not_5_out);
  and and_18 (and_18_out, d_ff_1_q[3], d_ff_7_q);
  and and_19 (and_19_out, d_ff_1_q[3], d_ff_8_q);
  and and_20 (and_20_out, j_k_ff_1_q, d_ff_5_q);
  or or_6 (or_6_out, and_20_out, and_24_out);
  or or_7 (or_7_out, and_16_out, and_17_out);
  and and_21 (and_21_out, d_ff_1_q[3], d_ff_10_q);
  and and_22 (and_22_out, d_ff_1_q[3], d_ff_11_q);
  J_K_Flip_Flop j_k_ff_3 (
    .J(or_7_out), .K(or_7_out), .clk(buffer_12_out), .Q(j_k_ff_2_q[1]), .Qn(j_k_ff_3_qn), .reset(or_8_out));  // open: preset
  or or_8 (or_8_out, and_39_out, and_36_out);
  and and_23 (and_23_out, d_ff_1_q[3], d_ff_12_q);
  and and_24 (and_24_out, not_4_out, d_ff_7_q);
  D_Flip_Flop d_ff_6 (.D(or_6_out), .clk(not_2_out), .Q(d_ff_6_q), .reset(reset_volume_out));  // open: Qn, preset
  and and_25 (and_25_out, and_16_out, j_k_ff_2_q[1]);
  and and_26 (and_26_out, j_k_ff_3_qn, and_17_out);
  or or_9 (or_9_out, and_25_out, and_26_out);
  assign and_27_out = j_k_ff_2_q & {4{d_ff_1_q[3]}};  // AND_Gate and_27, 4 bits wide
  assign and_28_out = j_k_ff_6_q & {4{d_ff_1_q[3]}};  // AND_Gate and_28, 4 bits wide
  J_K_Flip_Flop j_k_ff_4 (
    .J(or_9_out), .K(or_9_out), .clk(buffer_12_out), .Q(j_k_ff_2_q[2]), .Qn(j_k_ff_4_qn), .reset(or_10_out));  // open: preset
  or or_10 (or_10_out, and_39_out, and_36_out);
  and and_29 (and_29_out, j_k_ff_1_q, d_ff_6_q);
  and and_30 (and_30_out, and_25_out, j_k_ff_2_q[2]);
  and and_31 (and_31_out, j_k_ff_4_qn, and_26_out);
  and and_32 (and_32_out, not_4_out, d_ff_8_q);
  or or_11 (or_11_out, and_29_out, and_32_out);
  D_Flip_Flop d_ff_7 (.D(or_11_out), .clk(not_2_out), .Q(d_ff_7_q), .reset(reset_volume_out));  // open: Qn, preset
  J_K_Flip_Flop j_k_ff_5 (
    .J(or_12_out), .K(or_12_out), .clk(buffer_12_out), .Q(j_k_ff_2_q[3]), .reset(and_36_out));  // open: Qn, preset
  or or_12 (or_12_out, and_30_out, and_31_out);
  not not_6 (not_6_out, j_k_ff_2_q[3]);
  not not_7 (not_7_out, j_k_ff_2_q[2]);
  not not_8 (not_8_out, j_k_ff_2_q[1]);
  not not_9 (not_9_out, j_k_ff_2_q[0]);
  and and_33 (and_33_out, j_k_ff_1_q, d_ff_7_q);
  or or_13 (or_13_out, and_33_out, and_35_out);
  not not_10 (not_10_out, j_k_ff_2_q[0]);
  not not_11 (not_11_out, j_k_ff_2_q[2]);
  and and_34 (and_34_out, not_10_out, not_11_out);
  and and_35 (and_35_out, not_4_out, d_ff_10_q);
  D_Flip_Flop d_ff_8 (.D(or_13_out), .clk(not_2_out), .Q(d_ff_8_q), .reset(reset_volume_out));  // open: Qn, preset
  buf buffer_13 (buffer_13_out, j_k_ff_2_q[3]);
  and and_36 (and_36_out, and_34_out, and_38_out);
  and and_37 (and_37_out, not_9_out, nor_2_out, not_8_out, not_6_out, not_12_out, not_19_out, not_20_out, not_13_out, not_7_out);
  buf buffer_14 (buffer_14_out, j_k_ff_2_q[1]);
  and and_38 (and_38_out, buffer_13_out, buffer_14_out);
  and and_39 (and_39_out, and_38_out, and_40_out);
  not not_12 (not_12_out, j_k_ff_6_q[0]);
  buf buffer_15 (buffer_15_out, j_k_ff_2_q[2]);
  buf buffer_16 (buffer_16_out, j_k_ff_2_q[0]);
  and and_40 (and_40_out, buffer_15_out, buffer_16_out);
  not not_13 (not_13_out, j_k_ff_6_q[3]);
  not not_14 (not_14_out, j_k_ff_2_q[3]);
  not not_15 (not_15_out, j_k_ff_2_q[2]);
  not not_16 (not_16_out, j_k_ff_2_q[1]);
  and and_41 (and_41_out, not_14_out, not_15_out, not_16_out, not_17_out);
  or or_14 (or_14_out, and_39_out, and_36_out);
  and and_42 (and_42_out, j_k_ff_1_q, d_ff_8_q);
  not not_17 (not_17_out, j_k_ff_2_q[0]);
  and and_43 (and_43_out, and_41_out, and_55_out);
  D_Flip_Flop d_ff_9 (.Q(d_ff_9_q), .preset(and_43_out), .reset(buffer_12_out));  // open: D, clk, Qn
  and and_44 (and_44_out, not_4_out, d_ff_11_q);
  or or_15 (or_15_out, and_42_out, and_44_out);
  D_Flip_Flop d_ff_10 (.D(or_15_out), .clk(not_2_out), .Q(d_ff_10_q), .reset(reset_volume_out));  // open: Qn, preset
  J_K_Flip_Flop j_k_ff_6 (
    .J(d_ff_1_q[3]), .K(d_ff_1_q[3]), .clk(or_14_out), .Q(j_k_ff_6_q[0]), .Qn(j_k_ff_6_qn), .reset(and_57_out));  // open: preset
  not not_18 (not_18_out, nor_2_out);
  not not_19 (not_19_out, j_k_ff_6_q[1]);
  and and_45 (and_45_out, nor_2_out, j_k_ff_6_q[0]);
  and and_46 (and_46_out, j_k_ff_6_qn, not_18_out);
  or or_16 (or_16_out, and_45_out, and_46_out);
  and and_47 (and_47_out, j_k_ff_1_q, d_ff_10_q);
  J_K_Flip_Flop j_k_ff_7 (
    .J(or_16_out), .K(or_16_out), .clk(or_14_out), .Q(j_k_ff_6_q[1]), .Qn(j_k_ff_7_qn), .reset(or_17_out));  // open: preset
  or or_17 (or_17_out, and_57_out, and_59_out);
  not not_20 (not_20_out, j_k_ff_6_q[2]);
  and and_48 (and_48_out, not_4_out, d_ff_12_q);
  or or_18 (or_18_out, and_47_out, and_48_out);
  D_Flip_Flop d_ff_11 (.D(or_18_out), .clk(not_2_out), .Q(d_ff_11_q), .reset(reset_volume_out));  // open: Qn, preset
  and and_49 (and_49_out, and_45_out, j_k_ff_6_q[1]);
  and and_50 (and_50_out, j_k_ff_7_qn, and_46_out);
  or or_19 (or_19_out, and_49_out, and_50_out);
  J_K_Flip_Flop j_k_ff_8 (
    .J(or_19_out), .K(or_19_out), .clk(or_14_out), .Q(j_k_ff_6_q[2]), .Qn(j_k_ff_8_qn), .reset(or_20_out));  // open: preset
  or or_20 (or_20_out, and_57_out, and_59_out);
  and and_51 (and_51_out, j_k_ff_1_q, d_ff_11_q);
  or or_21 (or_21_out, and_51_out, and_54_out);
  not not_21 (not_21_out, j_k_ff_6_q[0]);
  and and_52 (and_52_out, and_49_out, j_k_ff_6_q[2]);
  and and_53 (and_53_out, j_k_ff_8_qn, and_50_out);
  and and_54 (and_54_out, not_4_out, in_1);
  D_Flip_Flop d_ff_12 (.D(or_21_out), .clk(not_2_out), .Q(d_ff_12_q), .reset(reset_volume_out));  // open: Qn, preset
  and and_55 (and_55_out, not_21_out, not_22_out, not_23_out, not_24_out);
  not not_22 (not_22_out, j_k_ff_6_q[1]);
  not not_23 (not_23_out, j_k_ff_6_q[2]);
  not not_24 (not_24_out, j_k_ff_6_q[3]);
  or or_22 (or_22_out, and_52_out, and_53_out);
  J_K_Flip_Flop j_k_ff_9 (
    .J(or_22_out), .K(or_22_out), .clk(or_14_out), .Q(j_k_ff_6_q[3]), .reset(and_57_out));  // open: Qn, preset
  not not_25 (not_25_out, j_k_ff_6_q[2]);
  not not_26 (not_26_out, j_k_ff_6_q[0]);
  and and_56 (and_56_out, not_25_out, not_26_out);
  and and_57 (and_57_out, and_56_out, and_58_out);
  buf buffer_17 (buffer_17_out, j_k_ff_6_q[3]);
  buf buffer_18 (buffer_18_out, j_k_ff_6_q[1]);
  and and_58 (and_58_out, buffer_17_out, buffer_18_out);
  buf buffer_19 (buffer_19_out, j_k_ff_6_q[2]);
  and and_59 (and_59_out, and_58_out, and_60_out);
  buf buffer_20 (buffer_20_out, j_k_ff_6_q[0]);
  and and_60 (and_60_out, buffer_19_out, buffer_20_out);
endmodule
