// Logisim project lab05.circ as structural Verilog: 1 circuit, main circuit main
module main (
  input  in_1,
  input  in_2,
  input  in_3,
  input  in_4,
  input  in_5,
  input  in_6,
  input  in_7,
  input  RIGHTLEFT,
  input  Datas_in,
  input  in_10,
  input  left_right,
  input  data_in,
  input  in_13,
  input  on_off,
  input  in_15
);

  wire and_1_out, and_2_out, and_3_out, and_4_out, and_5_out, and_6_out, and_7_out, and_8_out, and_9_out,
       and_10_out, and_11_out, and_12_out, and_13_out, and_14_out, and_15_out, and_16_out, and_17_out,
       and_18_out, and_19_out, and_20_out, and_21_out, and_22_out, and_23_out, and_24_out, and_25_out,
       and_26_out, and_27_out, and_28_out, and_29_out, and_30_out, and_31_out, and_32_out, and_33_out,
       and_34_out, and_35_out, and_36_out, and_37_out, and_38_out, and_39_out, and_40_out, and_41_out,
       button_1_out, button_2_out, button_3_out, clock_1_out, clock_2_out, d_ff_1_q, d_ff_2_q, d_ff_3_q,
       d_ff_4_q, d_ff_5_q, d_ff_6_q, d_ff_7_q, d_ff_8_q, d_ff_9_q, d_ff_10_q, d_ff_11_q, d_ff_12_q,
       d_ff_13_q, d_ff_14_q, d_ff_15_q, d_ff_16_q, d_ff_17_q, not_1_out, not_2_out, not_3_out, not_4_out,
       not_5_out, not_6_out, or_1_out, or_2_out, or_3_out, or_4_out, or_5_out, or_6_out, or_7_out, or_8_out,
       or_9_out, or_10_out, or_11_out, or_12_out, or_13_out, reset_out, undriven;

  Button button_1 (.out(button_1_out));
  Button reset (.out(reset_out));
  not not_1 (not_1_out, in_3);
  not not_2 (not_2_out, in_6);
  not not_3 (not_3_out, in_7);
  not not_4 (not_4_out, left_right);
  and and_1 (and_1_out, left_right, data_in);
  and and_2 (and_2_out, not_2_out, not_3_out);
  and and_3 (and_3_out, not_2_out, in_7);
  and and_4 (and_4_out, in_6, not_3_out);
  and and_5 (and_5_out, in_6, in_7);
  and and_6 (and_6_out, not_4_out, d_ff_4_q);
  or or_1 (or_1_out, and_1_out, and_6_out);
  D_Flip_Flop d_ff_1 (.D(or_1_out), .clk(button_1_out), .Q(d_ff_1_q), .reset(reset_out));  // open: Qn, preset
  LED led_1 (.in(and_2_out));
  LED led_2 (.in(and_3_out));
  LED led_3 (.in(and_4_out));
  LED led_4 (.in(and_5_out));
  and and_7 (and_7_out, button_1_out, in_15);
  or or_2 (or_2_out, in_2, in_3);
  and and_8 (and_8_out, not_1_out, in_1);
  Clock clock_1 (.out(clock_1_out));
  Button button_2 (.out(button_2_out));
  and and_9 (and_9_out, d_ff_1_q, on_off);
  and and_10 (and_10_out, d_ff_1_q, in_15);
  or or_3 (or_3_out, in_2, and_8_out);
  not not_5 (not_5_out, RIGHTLEFT);
  and and_11 (and_11_out, RIGHTLEFT, Datas_in);
  LED led_5 (.in(and_9_out));
  D_Flip_Flop d_ff_2 (.D(and_10_out), .clk(and_7_out), .Q(d_ff_2_q));  // open: Qn, preset, reset
  LED led_6 (.in(or_2_out));
  LED led_7 (.in(or_3_out));
  and and_12 (and_12_out, not_5_out, d_ff_5_q);
  or or_4 (or_4_out, and_11_out, and_12_out);
  D_Flip_Flop d_ff_3 (.D(or_4_out), .clk(clock_1_out), .Q(d_ff_3_q), .reset(button_2_out));  // open: Qn, preset
  and and_13 (and_13_out, left_right, d_ff_1_q);
  and and_14 (and_14_out, not_4_out, d_ff_6_q);
  or or_5 (or_5_out, and_13_out, and_14_out);
  D_Flip_Flop d_ff_4 (.D(or_5_out), .clk(button_1_out), .Q(d_ff_4_q), .reset(reset_out));  // open: Qn, preset
  LED led_8 (.in(d_ff_3_q));
  LED led_9 (.in(d_ff_2_q));
  and and_15 (and_15_out, d_ff_4_q, on_off);
  and and_16 (and_16_out, RIGHTLEFT, d_ff_3_q);
  LED led_10 (.in(and_15_out));
  and and_17 (and_17_out, not_5_out, d_ff_9_q);
  or or_6 (or_6_out, and_16_out, and_17_out);
  D_Flip_Flop d_ff_5 (.D(or_6_out), .clk(clock_1_out), .Q(d_ff_5_q), .reset(button_2_out));  // open: Qn, preset
  and and_18 (and_18_out, left_right, d_ff_4_q);
  and and_19 (and_19_out, not_4_out, d_ff_10_q);
  or or_7 (or_7_out, and_18_out, and_19_out);
  D_Flip_Flop d_ff_6 (.D(or_7_out), .clk(button_1_out), .Q(d_ff_6_q), .reset(reset_out));  // open: Qn, preset
  and and_20 (and_20_out, d_ff_4_q, in_15);
  and and_21 (and_21_out, button_1_out, in_15);
  LED led_11 (.in(d_ff_5_q));
  D_Flip_Flop d_ff_7 (.D(and_20_out), .clk(and_21_out), .Q(d_ff_7_q));  // open: Qn, preset, reset
  not not_6 (not_6_out, in_5);
  and and_22 (and_22_out, d_ff_6_q, on_off);
  Clock clock_2 (.out(clock_2_out));
  Button button_3 (.out(button_3_out));
  and and_23 (and_23_out, RIGHTLEFT, d_ff_5_q);
  LED led_12 (.in(and_22_out));
  LED led_13 (.in(d_ff_7_q));
  D_Flip_Flop d_ff_8 (.D(not_6_out), .clk(clock_2_out), .Q(d_ff_8_q), .reset(button_3_out));  // open: Qn, preset
  and and_24 (and_24_out, not_5_out, d_ff_13_q);
  or or_8 (or_8_out, and_23_out, and_24_out);
  D_Flip_Flop d_ff_9 (.D(or_8_out), .clk(clock_1_out), .Q(d_ff_9_q), .reset(button_2_out));  // open: Qn, preset
  and and_25 (and_25_out, left_right, d_ff_6_q);
  LED led_14 (.in(d_ff_8_q));
  LED led_15 (.in(d_ff_9_q));
  and and_26 (and_26_out, not_4_out, d_ff_14_q);
  or or_9 (or_9_out, and_25_out, and_26_out);
  D_Flip_Flop d_ff_10 (.D(or_9_out), .clk(button_1_out), .Q(d_ff_10_q), .reset(reset_out));  // open: Qn, preset
  and and_27 (and_27_out, d_ff_6_q, in_15);
  D_Flip_Flop d_ff_11 (.D(and_27_out), .clk(and_28_out), .Q(d_ff_11_q));  // open: Qn, preset, reset
  and and_28 (and_28_out, button_1_out, in_15);
  and and_29 (and_29_out, d_ff_10_q, on_off);
  LED led_16 (.in(d_ff_11_q));
  and and_30 (and_30_out, d_ff_8_q, in_5);
  D_Flip_Flop d_ff_12 (.D(or_10_out), .clk(clock_2_out), .Q(d_ff_12_q), .reset(button_3_out));  // open: Qn, preset
  and and_31 (and_31_out, RIGHTLEFT, d_ff_9_q);
  LED led_17 (.in(and_29_out));
  or or_10 (or_10_out, and_30_out, and_35_out);
  and and_32 (and_32_out, not_5_out, d_ff_16_q);
  or or_11 (or_11_out, and_31_out, and_32_out);
  D_Flip_Flop d_ff_13 (.D(or_11_out), .clk(clock_1_out), .Q(d_ff_13_q), .reset(button_2_out));  // open: Qn, preset
  and and_33 (and_33_out, left_right, d_ff_10_q);
  or or_12 (or_12_out, and_33_out, and_36_out);
  and and_34 (and_34_out, d_ff_10_q, in_15);
  and and_35 (and_35_out, not_6_out, not_6_out);
  LED led_18 (.in(d_ff_12_q));
  LED led_19 (.in(d_ff_13_q));
  and and_36 (and_36_out, not_4_out, in_13);
  D_Flip_Flop d_ff_14 (.D(or_12_out), .clk(button_1_out), .Q(d_ff_14_q), .reset(reset_out));  // open: Qn, preset
  D_Flip_Flop d_ff_15 (.D(and_34_out), .clk(and_37_out), .Q(d_ff_15_q));  // open: Qn, preset, reset
  and and_37 (and_37_out, in_15, button_1_out);
  and and_38 (and_38_out, d_ff_14_q, on_off);
  LED led_20 (.in(and_38_out));
  LED led_21 (.in(d_ff_15_q));
  and and_39 (and_39_out, RIGHTLEFT, d_ff_13_q);
  or or_13 (or_13_out, and_39_out, and_40_out);
  and and_40 (and_40_out, not_5_out, in_10);
  D_Flip_Flop d_ff_16 (.D(or_13_out), .clk(clock_1_out), .Q(d_ff_16_q), .reset(button_2_out));  // open: Qn, preset
  and and_41 (and_41_out, d_ff_14_q, in_15);
  LED led_22 (.in(d_ff_16_q));
  D_Flip_Flop d_ff_17 (.D(and_41_out), .clk(undriven), .Q(d_ff_17_q));  // open: Qn, preset, reset
  LED led_23 (.in(d_ff_17_q));
endmodule
